# Fritzing sketch fritzing_diagram (saved by Fritzing 0.9.2b)
circuit board: 8.46667cm x 5.64444cm
breadboards: 2

parts:
  RHT1 = Humidity and Temperature Sensor RHT03
  Pi1 = Adafruit Pi Cobbler
  LED1 = RGB LED (com. cathode, rgb) [package="5 mm [THT]"]
  R1 = Resistor [tolerance=±5% resistance=220 package=THT]
  R2 = Resistor [tolerance=±5% resistance=100 package=THT]
  R4 = Resistor [tolerance=±5% resistance=220 package=THT]
  R5 = Resistor [tolerance=±5% resistance=6.8k package=THT]
  S1 = Pushbutton [package="[THT]"]

nets:
  N1: RHT1.Vcc, Pi1.5V0, LED1.green_anode, R5.Pin_0, S1.Pin_3, S1.Pin_4
  N2: RHT1.Data-signal, Pi1.#18, R5.Pin_1
  N3: RHT1.GND_2, Pi1.GND
  N4: Pi1.#17, S1.Pin_1, S1.Pin_2
  N5: Pi1.#23, R1.Pin_1
  N6: Pi1.#24, R2.Pin_1
  N7: Pi1.#25, R4.Pin_1
  N8: LED1.red_anode, R1.Pin_0
  N9: LED1.common_cathode, R2.Pin_0
  N10: LED1.blue_anode, R4.Pin_0

custom parts:
  Adafruit Pi Cobbler: Adafruit Pi Cobbler GPIO Breakout for Raspberry Pi
